// Logisim project controle.circ as structural Verilog: 1 circuit, main circuit controle
module controle (
  input  [5:0] INSTR_CLASS_5_0,
  input  CLK,
  input  RESET,
  input  DF,
  input  Q_IN,
  input  [3:0] EF_3_0,
  input  D_ZERO,
  output [3:0] ALU_OP_3_0,
  output [2:0] SRC_A_2_0,
  output [2:0] SRC_B_2_0,
  output [3:0] DST_3_0,
  output [2:0] ADDR_SRC_2_0,
  output [3:0] REG_SEL_SRC_3_0,
  output MEM_RD,
  output MEM_WR,
  output IR_LOAD,
  output REG_INC,
  output REG_DEC,
  output DF_LOAD,
  output Q_LOAD,
  output COND_EN,
  output [2:0] NEXT_STATE_2_0,
  output [2:0] ESTADO_OUT_2_0
);

  wire [2:0] undriven_2;
  wire [5:0] undriven;
  wire [31:12] undriven_3;

  // Register #(.width(3)) REG_ESTADO: pin names not known; wires that end beside it: CLK, NEXT_STATE_2_0, RESET
  ROM #(.addrWidth(9), .dataWidth(32)) uROM (.addr({undriven_2, undriven}));  // open: data
  // Pins of 1 and 4 bits meet at {undriven_3[31:29], IR_LOAD}
  // Pins of 1 and 3 bits meet at {undriven_3[27:26], REG_INC}
  // Pins of 1 and 3 bits meet at {undriven_3[24:23], REG_DEC}
  // Pins of 1 and 4 bits meet at {undriven_3[21:19], DF_LOAD}
  // Pins of 1 and 3 bits meet at {undriven_3[17:16], Q_LOAD}
  // Pins of 1 and 4 bits meet at {undriven_3[14:12], COND_EN}
  // Pins of 1 and 3 bits meet at NEXT_STATE_2_0
endmodule
