// Logisim project rca.circ as structural Verilog: 1 circuit, main circuit main
module main (
  input  in_1,
  input  in_2
);

  wire banco_1_p4, banco_1_p8, banco_1_p9, banco_1_p16, banco_1_p22, banco_1_p23, banco_1_p25, banco_1_p26,
       banco_1_p27, clock_1_out, comparator_1_eq, controle_1_p4, controle_1_p5, decoder_1_out1,
       decoder_1_out3, decoder_1_out4, decoder_1_out5, decoder_1_out6, decoder_1_out7, decoder_1_out8,
       decoder_1_out9, decoder_1_out10, or_1_out;
  wire [1:0] banco_1_p14;
  wire [2:0] undriven;
  wire [2:2] controle_1_p7;
  wire [3:0] banco_1_p10, banco_1_p17, controle_1_p8;
  wire [5:0] pla_decoder_1_instr_class;
  wire [7:0] banco_1_p6, banco_1_p24, memoria_io_1_p7;
  wire [15:0] bit_extender_1_out;

  Decoder #(.enable("false"), .select(4)) decoder_1 (
    .out1(decoder_1_out1), .out3(decoder_1_out3), .out4(decoder_1_out4), .out5(decoder_1_out5),
    .out6(decoder_1_out6), .out7(decoder_1_out7), .out8(decoder_1_out8), .out9(decoder_1_out9),
    .out10(decoder_1_out10), .sel(controle_1_p8));  // open: out0, out2, out11, out12, out13, out14, out15
  or or_1 (or_1_out, decoder_1_out3, decoder_1_out4, decoder_1_out5, decoder_1_out6);
  assign bit_extender_1_out = {{8{1'b0}}, memoria_io_1_p7};  // Bit_Extender bit_extender_1
  Clock clock_1 (.out(clock_1_out));
  // Banco banco_1: pin names not known; wires that end beside it: in_2, clock_1_out, bit_extender_1_out, banco_1_p4, or_1_out, banco_1_p6, decoder_1_out1, banco_1_p8, banco_1_p9, banco_1_p10, decoder_1_out7, banco_1_p10, decoder_1_out8, banco_1_p14, banco_1_p10, banco_1_p16, banco_1_p17, banco_1_p16, banco_1_p6, decoder_1_out9, decoder_1_out10, banco_1_p22, banco_1_p23, banco_1_p24, banco_1_p25, banco_1_p26, banco_1_p27
  // controle controle_1: pin names not known; wires that end beside it: banco_1_p22, banco_1_p9, banco_1_p16, controle_1_p4, controle_1_p5, banco_1_p4, {controle_1_p7[2], banco_1_p14}, controle_1_p8
  Comparator comparator_1 (.a({8{1'b0}}), .b(banco_1_p24), .eq(comparator_1_eq));  // open: gt, lt
  ALU alu_1 (
    .Bus_In(memoria_io_1_p7), .D(banco_1_p24), .Data_Flag(banco_1_p26), .Alu_Op(undriven),
    .Shifter_Direction(undriven[1]), .Alu_Out(banco_1_p6), .Flag_Out(banco_1_p8));
  PLA_decoder pla_decoder_1 (
    .OPCODE(memoria_io_1_p7), .INSTR_CLASS(pla_decoder_1_instr_class), .N(banco_1_p10), .I(banco_1_p17));
  // memoria_io memoria_io_1: pin names not known; wires that end beside it: in_1, banco_1_p23, controle_1_p4, controle_1_p5, banco_1_p6, banco_1_p25, memoria_io_1_p7
endmodule
